// Logisim project Team_30.circ as structural Verilog: 3 circuits, main circuit main
module main (
  output E
);

  wire clock_1_out, cu_1_ac_load, cu_1_ar_load, cu_1_dr_load, cu_1_ir_load, cu_1_memory_load,
       cu_1_memory_store, cu_1_pc_clr, cu_1_pc_inc, cu_1_pc_load, cu_1_tr_load, decoder_1_out0,
       decoder_1_out1, decoder_1_out2, decoder_1_out3, decoder_1_out4, decoder_1_out5, decoder_1_out6,
       or_1_out, Reset_out;
  wire [2:0] cu_1_alu_control, cu_1_bus;
  wire [5:0] AR_q, bit_extender_1_out, bit_extender_2_out, PC_q;
  wire [15:0] AC_q, alu_1_out_5, bit_extender_3_out, bit_extender_4_out, controlled_buffer_1_out, DR_q, IR_q,
       ram_1_data, TR_q;

  CU cu_1 (
    .IR_Register(IR_q), .AC_Register(AC_q), .BUS(cu_1_bus), .ALU_control(cu_1_alu_control),
    .Memory_Load(cu_1_memory_load), .Memory_Store(cu_1_memory_store), .AR_load(cu_1_ar_load),
    .IR_load(cu_1_ir_load), .PC_inc(cu_1_pc_inc), .PC_Load(cu_1_pc_load), .PC_CLR(cu_1_pc_clr),
    .DR_load(cu_1_dr_load), .AC_Load(cu_1_ac_load), .CLK(clock_1_out), .Reset(Reset_out),
    .TR_Load(cu_1_tr_load));
  Button Reset (.out(Reset_out));
  Bit_Extender #(.in_width(16), .out_width(6)) bit_extender_1 (.in(controlled_buffer_1_out), .out(bit_extender_1_out));
  ALU alu_1 (.out_4(E), .out_5(alu_1_out_5), .A(DR_q), .B(AC_q), .in_3(cu_1_alu_control));
  Bit_Extender #(.in_width(16), .out_width(6)) bit_extender_2 (.in(controlled_buffer_1_out), .out(bit_extender_2_out));
  RAM #(.addrWidth(6), .dataWidth(16), .bus("separate")) ram_1 (
    .addr(AR_q), .din(controlled_buffer_1_out), .data(ram_1_data), .str(cu_1_memory_store),
    .clk(clock_1_out), .ld(cu_1_memory_load), .clr(Reset_out));  // open: sel
  Register #(.width(6)) AR (.D(bit_extender_1_out), .en(cu_1_ar_load), .Q(AR_q), .clk(clock_1_out), .clr(Reset_out));
  Register #(.width(16)) DR (
    .D(controlled_buffer_1_out), .en(cu_1_dr_load), .Q(DR_q), .clk(clock_1_out), .clr(Reset_out));
  Register #(.width(16)) AC (.D(alu_1_out_5), .en(cu_1_ac_load), .Q(AC_q), .clk(clock_1_out), .clr(Reset_out));
  Register #(.width(16)) TR (
    .D(controlled_buffer_1_out), .en(cu_1_tr_load), .Q(TR_q), .clk(clock_1_out), .clr(Reset_out));
  Counter #(.width(6), .max('h3f)) PC (
    .load(cu_1_pc_load), .D(bit_extender_2_out), .count(cu_1_pc_inc), .Q(PC_q), .clk(clock_1_out),
    .clr(or_1_out));  // open: carry
  or or_1 (or_1_out, cu_1_pc_clr, Reset_out);
  Register #(.width(16)) IR (
    .D(controlled_buffer_1_out), .en(cu_1_ir_load), .Q(IR_q), .clk(clock_1_out), .clr(Reset_out));
  Decoder #(.select(3), .enable("false")) decoder_1 (
    .out0(decoder_1_out0), .out1(decoder_1_out1), .out2(decoder_1_out2), .out3(decoder_1_out3),
    .out4(decoder_1_out4), .out5(decoder_1_out5), .out6(decoder_1_out6), .sel(cu_1_bus));  // open: out7
  assign bit_extender_3_out = {{10{1'b0}}, AR_q};  // Bit_Extender bit_extender_3
  assign bit_extender_4_out = {{10{1'b0}}, PC_q};  // Bit_Extender bit_extender_4
  Clock clock_1 (.out(clock_1_out));
  assign controlled_buffer_1_out = decoder_1_out4 ? ram_1_data : 16'bz;  // Controlled_Buffer controlled_buffer_1
  assign controlled_buffer_1_out = decoder_1_out3 ? bit_extender_3_out : 16'bz;  // Controlled_Buffer controlled_buffer_2
  assign controlled_buffer_1_out = decoder_1_out1 ? DR_q : 16'bz;  // Controlled_Buffer controlled_buffer_3
  assign controlled_buffer_1_out = decoder_1_out0 ? AC_q : 16'bz;  // Controlled_Buffer controlled_buffer_4
  assign controlled_buffer_1_out = decoder_1_out2 ? TR_q : 16'bz;  // Controlled_Buffer controlled_buffer_5
  assign controlled_buffer_1_out = decoder_1_out5 ? bit_extender_4_out : 16'bz;  // Controlled_Buffer controlled_buffer_6
  assign controlled_buffer_1_out = decoder_1_out6 ? IR_q : 16'bz;  // Controlled_Buffer controlled_buffer_7
endmodule

module ALU (
  input  [15:0] A,
  input  [15:0] B,
  input  [2:0] in_3,
  output out_4,
  output [15:0] out_5
);

  wire adder_1_cout, not_2_out, or_2_out, subtractor_1_bout;
  wire [15:0] adder_1_out, and_1_out, not_1_out, or_1_out, subtractor_1_out, xor_1_out;

  assign not_1_out = ~B;  // NOT_Gate not_1, 16 bits wide
  Adder #(.width(16)) adder_1 (.a(B), .b(A), .out(adder_1_out), .cout(adder_1_cout));  // open: cin
  Subtractor #(.width(16)) subtractor_1 (.a(B), .b(A), .out(subtractor_1_out), .bout(subtractor_1_bout));  // open: bin
  assign and_1_out = B & A;  // AND_Gate and_1, 16 bits wide
  assign or_1_out = B | A;  // OR_Gate or_1, 16 bits wide
  assign xor_1_out = B ^ A;  // XOR_Gate xor_1, 16 bits wide
  Multiplexer #(.select(3), .width(16), .enable("false")) multiplexer_1 (
    .in0(adder_1_out), .in1(subtractor_1_out), .in2(A), .in3(and_1_out), .in4(or_1_out), .in5(xor_1_out),
    .in6(not_1_out), .out(out_5), .sel(in_3));  // open: in7
  Multiplexer multiplexer_2 (.in0(adder_1_cout), .in1(subtractor_1_bout), .out(out_4), .sel(in_3[0]), .en(not_2_out));
  not not_2 (not_2_out, or_2_out);
  or or_2 (or_2_out, in_3[1], in_3[2]);
endmodule

module CU (
  input  [15:0] IR_Register,
  input  [15:0] AC_Register,
  input  CLK,
  input  Reset,
  output [2:0] BUS,
  output [2:0] ALU_control,
  output Memory_Load,
  output Memory_Store,
  output AR_load,
  output IR_load,
  output TR_Load,
  output PC_inc,
  output PC_Load,
  output PC_CLR,
  output DR_load,
  output AC_Load
);

  wire and_1_out, and_2_out, and_3_out, and_4_out, and_5_out, and_6_out, and_7_out, and_8_out, and_9_out,
       and_10_out, and_11_out, and_12_out, and_13_out, CLR_out, D0_D1_D2_D5_out, D7_prime_IT3_out, d_ff_1_q,
       decoder_1_out0, decoder_1_out1, decoder_1_out2, decoder_1_out3, decoder_1_out4, decoder_1_out5,
       decoder_1_out6, decoder_1_out7, decoder_2_out0, decoder_2_out1, decoder_2_out2, decoder_2_out3,
       decoder_2_out4, decoder_2_out5, decoder_2_out6, decoder_2_out7, decoder_2_out8, decoder_2_out9,
       decoder_2_out10, decoder_2_out11, decoder_2_out12, decoder_2_out13, decoder_2_out14, decoder_2_out15,
       I_q, I_qn, nor_1_out, not_1_out, not_2_out, or_1_out, or_2_out, or_3_out, or_4_out, r_out, Set_out;
  wire [3:0] counter_1_q;

  Decoder #(.select(3), .enable("false")) decoder_1 (
    .out0(decoder_1_out0), .out1(decoder_1_out1), .out2(decoder_1_out2), .out3(decoder_1_out3),
    .out4(decoder_1_out4), .out5(decoder_1_out5), .out6(decoder_1_out6), .out7(decoder_1_out7),
    .sel(IR_Register[14:12]));
  Button Set (.out(Set_out));
  D_Flip_Flop I (.clk(CLK), .D(IR_Register[15]), .Q(I_q), .Qn(I_qn), .preset(Set_out), .en(1'b1), .reset(CLR_out));
  Button CLR (.out(CLR_out));
  Counter #(.width(4), .max('hf)) counter_1 (
    .Q(counter_1_q), .clk(CLK), .clr(or_1_out));  // open: load, D, count, carry
  or or_1 (or_1_out, Reset, d_ff_1_q);
  D_Flip_Flop d_ff_1 (.clk(CLK), .D(or_2_out), .Q(d_ff_1_q), .en(1'b1));  // open: Qn, preset, reset
  or or_2 (or_2_out, and_1_out, and_3_out, and_2_out);
  and r (r_out, decoder_1_out7, I_qn, decoder_2_out3);
  Decoder #(.select(4), .enable("false")) decoder_2 (
    .out0(decoder_2_out0), .out1(decoder_2_out1), .out2(decoder_2_out2), .out3(decoder_2_out3),
    .out4(decoder_2_out4), .out5(decoder_2_out5), .out6(decoder_2_out6), .out7(decoder_2_out7),
    .out8(decoder_2_out8), .out9(decoder_2_out9), .out10(decoder_2_out10), .out11(decoder_2_out11),
    .out12(decoder_2_out12), .out13(decoder_2_out13), .out14(decoder_2_out14), .out15(decoder_2_out15),
    .sel(counter_1_q));
  or or_3 (or_3_out, AC_Register[7], AC_Register[0], AC_Register[1], AC_Register[2], AC_Register[3], AC_Register[4], AC_Register[5], AC_Register[6], AC_Register[8], AC_Register[9], AC_Register[10], AC_Register[11], AC_Register[12], AC_Register[13], AC_Register[14], AC_Register[15]);
  and and_1 (and_1_out, or_4_out, decoder_2_out5);
  and and_2 (and_2_out, decoder_1_out3, decoder_2_out4);
  or or_4 (or_4_out, decoder_1_out0, decoder_1_out1, decoder_1_out2, decoder_1_out4, decoder_1_out5);
  and and_3 (and_3_out, IR_Register[2], r_out);
  not not_1 (not_1_out, or_3_out);
  LED Not_Memory (.in(decoder_1_out7));
  and and_4 (and_4_out, r_out, IR_Register[2], not_1_out);
  and and_5 (and_5_out, decoder_1_out7, I_q);
  LED I_O (.in(and_5_out));
  LED Register (.in(and_6_out));
  and and_6 (and_6_out, I_qn, decoder_1_out7);
  and and_7 (and_7_out, decoder_2_out4, decoder_1_out3);
  not not_2 (not_2_out, decoder_1_out7);
  and and_8 (and_8_out, decoder_2_out5, decoder_1_out4);
  and D7_prime_IT3 (D7_prime_IT3_out, I_q, not_2_out, decoder_2_out3);
  or D0_D1_D2_D5 (D0_D1_D2_D5_out, decoder_1_out0, decoder_1_out1, decoder_1_out2, decoder_1_out5);
  nor nor_1 (nor_1_out, and_7_out, and_8_out, decoder_2_out2, Memory_Load, decoder_2_out0);
  and and_9 (and_9_out, D0_D1_D2_D5_out, decoder_2_out4);
  or or_5 (Memory_Load, decoder_2_out1, D7_prime_IT3_out, and_9_out);
  and and_10 (and_10_out, D0_D1_D2_D5_out, decoder_2_out5);
  Priority_Encoder priority_encoder_1 (
    .in0(and_7_out), .in1(1'b0), .in2(1'b0), .in3(and_8_out), .in4(Memory_Load), .in5(decoder_2_out0),
    .in6(decoder_2_out2), .in7(nor_1_out), .out(BUS), .en_in(1'b1));  // open: gs, en_out
  and and_11 (and_11_out, decoder_1_out3, decoder_2_out4);
  and and_12 (and_12_out, decoder_1_out4, decoder_2_out5);
  and and_13 (and_13_out, decoder_1_out4, decoder_2_out4);
  buf or_6 (DR_load, and_9_out);  // OR_Gate
  buf or_7 (AC_Load, and_10_out);  // OR_Gate
  buf or_8 (Memory_Store, and_11_out);  // OR_Gate
  or or_9 (AR_load, decoder_2_out0, decoder_2_out2, D7_prime_IT3_out);
  buf or_10 (IR_load, decoder_2_out1);  // OR_Gate
  or or_11 (PC_inc, decoder_2_out1, and_4_out);
  buf or_12 (PC_Load, and_12_out);  // OR_Gate
  buf or_13 (PC_CLR, and_13_out);  // OR_Gate
  or or_14 (ALU_control[0], decoder_1_out0, decoder_1_out5);
  or or_15 (ALU_control[1], decoder_1_out2, decoder_1_out0);

  assign ALU_control[2] = 1'b0;
  assign TR_Load = 1'b0;
endmodule
